# Fritzing sketch Automated_Curtains_Schematic (saved by Fritzing 0.9.3b)
breadboards: 1

parts:
  U1 = Voltage Regulator - 5V [package="TO220 [THT]"]
  U2 = Voltage Regulator - 3.3V [package="TO220 [THT]"]
  Power_plug1 = Power plug
  J1 = female pin header, 3 pins [form="♀ (female)"]
  J2 = female pin header, 2 pins [form="♀ (female)"]
  Part1 = Arduino Nano (Rev3.0)
  J3 = Basic Servo
  J4 = female pin header, 3 pins [form="♀ (female)"]
  S1 = Pushbutton [package="[THT]"]
  R1 = Resistor [tolerance=±5% resistance=220 package=THT]
  R2 = Resistor [tolerance=±5% resistance=220 package=THT]
  U3 = ESP8266 WiFi Module [part_number=ESP8266]
  S2 = Pushbutton [package="[THT]"]

nets:
  N1: U1.input_voltage, U2.input_voltage, Power_plug1.VCC
  GND: U1.GND, U2.GND, Power_plug1.GND, J2.pin2, Part1.GND, J3.gnd, J4.pin2, R1.Pin_1, R2.Pin_1, U3.GND
  VIN: U1.output_voltage, Part1.VIN, J3.vcc, J4.pin1, S1.Pin_3, S1.Pin_4, S2.Pin_3, S2.Pin_4
  N2: U2.output_voltage, J1.pin1, J1.pin2, J1.pin3, U3.VCC, U3.RST, U3.CH_PD
  N3: J2.pin1, Part1.D12/MISO, U3.GPIO_2
  N4: Part1.D3, S1.Pin_1, S1.Pin_2, R2.Pin_0
  N5: Part1.D4, R1.Pin_0, S2.Pin_1, S2.Pin_2
  N6: Part1.D9, J3.pulse, J4.pin3

custom parts:
  ESP8266 WiFi Module: Generic WiFi Module based on the ESP8266 with onboard PCB antenna and UART communications
